# Fritzing sketch decay_calculator (saved by Fritzing 0.9.3b)

parts:
  LCM1602_IIC2 = LCM1602 IIC [part_number="LCM1602 IIC" chip_label="LCM1602 IIC" package="DIP (Dual Inline) [THT]"]
  LCD4 = LCD screen
  Raspberry_Pi2 = Raspberry Pi Zero
  X1 = DB9 Connector [package=db9]

nets:
  VSS: LCM1602_IIC2.VSS, LCD4.VSS
  VDD: LCM1602_IIC2.VDD, LCD4.VDD
  N1: LCM1602_IIC2.V0, LCD4.V0
  N2: LCM1602_IIC2.RS, LCD4.RS
  N3: LCM1602_IIC2.RW, LCD4.R/W
  N4: LCM1602_IIC2.E, LCD4.E
  N5: LCM1602_IIC2.D0, LCD4.DB0
  N6: LCM1602_IIC2.D1, LCD4.DB1
  N7: LCM1602_IIC2.D2, LCD4.DB2
  N8: LCM1602_IIC2.D3, LCD4.DB3
  N9: LCM1602_IIC2.D4, LCD4.DB4
  N10: LCM1602_IIC2.D5, LCD4.DB5
  N11: LCM1602_IIC2.D6, LCD4.DB6
  N12: LCM1602_IIC2.D7, LCD4.DB7
  N13: LCM1602_IIC2.A, LCD4.LED+
  N14: LCM1602_IIC2.K, LCD4.LED-
  GND: LCM1602_IIC2.GND, Raspberry_Pi2.GND, X1.5
  VCC: LCM1602_IIC2.VCC, Raspberry_Pi2.5V
  N15: LCM1602_IIC2.SDA, Raspberry_Pi2.GPIO2
  N16: LCM1602_IIC2.SCL, Raspberry_Pi2.GPIO3
  N17: LCM1602_IIC2.LED_A, LCM1602_IIC2.LED_B
  N18: Raspberry_Pi2.GIPO15, X1.3
  N19: Raspberry_Pi2.GIPO14, X1.2

notes:
  to USB Keypad
  to dose calibrator

custom parts:
  LCM1602 IIC: I2C-Module to use a 1602 or 2004 LCD on with the wire.h libory Serial LCD Modul
  Raspberry Pi Zero: The Raspberry Pi Zero is the latest single board computer to be released by the Raspberry Pi Foundation. It is the entry level model Raspberry Pi perfect for hobbyists, makers and industrial engineers looking to create solutions where small size and low power consumption are important. This is especially relevant for applications in the wearables space as well as up and coming applications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
